// Digital circuit AsynchronousCounter.dig as structural Verilog
module AsynchronousCounter (
  input  CLK,
  input  CLR,
  output [7:0] COUNT
);

  wire d_ff_as_1_nq, d_ff_as_2_nq, d_ff_as_3_nq, d_ff_as_4_nq, d_ff_as_5_nq, d_ff_as_6_nq, d_ff_as_7_nq,
       d_ff_as_8_nq, or_1_out, reset_1_out;

  or or_1 (or_1_out, CLR, reset_1_out);
  D_FF_AS d_ff_as_1 (.Set(1'b0), .D(d_ff_as_1_nq), .C(CLK), .Clr(or_1_out), .Q(COUNT[0]), .nQ(d_ff_as_1_nq));
  Reset #(.invertOutput("false")) reset_1 (.out(reset_1_out));
  D_FF_AS d_ff_as_2 (.Set(1'b0), .D(d_ff_as_2_nq), .C(d_ff_as_1_nq), .Clr(or_1_out), .Q(COUNT[1]), .nQ(d_ff_as_2_nq));
  D_FF_AS d_ff_as_3 (.Set(1'b0), .D(d_ff_as_3_nq), .C(d_ff_as_2_nq), .Clr(or_1_out), .Q(COUNT[2]), .nQ(d_ff_as_3_nq));
  D_FF_AS d_ff_as_4 (.Set(1'b0), .D(d_ff_as_4_nq), .C(d_ff_as_3_nq), .Clr(or_1_out), .Q(COUNT[3]), .nQ(d_ff_as_4_nq));
  D_FF_AS d_ff_as_5 (.Set(1'b0), .D(d_ff_as_5_nq), .C(d_ff_as_4_nq), .Clr(or_1_out), .Q(COUNT[4]), .nQ(d_ff_as_5_nq));
  D_FF_AS d_ff_as_6 (.Set(1'b0), .D(d_ff_as_6_nq), .C(d_ff_as_5_nq), .Clr(or_1_out), .Q(COUNT[5]), .nQ(d_ff_as_6_nq));
  D_FF_AS d_ff_as_7 (.Set(1'b0), .D(d_ff_as_7_nq), .C(d_ff_as_6_nq), .Clr(or_1_out), .Q(COUNT[6]), .nQ(d_ff_as_7_nq));
  D_FF_AS d_ff_as_8 (.Set(1'b0), .D(d_ff_as_8_nq), .C(d_ff_as_7_nq), .Clr(or_1_out), .Q(COUNT[7]), .nQ(d_ff_as_8_nq));
endmodule
