// Digital circuit BabylonianAlarm.dig as structural Verilog
module BabylonianAlarm (
  input  CLR,
  input  SETUP,
  input  MIN_ADV,
  input  HR_ADV,
  output [5:0] MINUTES,
  output [4:0] HOURS
);

  wire and_1_out, and_2_out, and_3_out, and_4_out, or_1_out, or_2_out, or_3_out, or_4_out;

  and and_1 (and_1_out, MIN_ADV, SETUP);
  or or_1 (or_1_out, and_1_out, CLR);
  or or_2 (or_2_out, CLR, and_2_out);
  Counter #(.Bits(6)) MINUTES_COUNTER (.en(1'b1), .C(or_1_out), .clr(or_2_out), .out(MINUTES));  // open: ovf
  and and_2 (and_2_out, MINUTES[0], MINUTES[1], MINUTES[3], MINUTES[4], MINUTES[5]);
  or or_3 (or_3_out, and_3_out, CLR);
  or or_4 (or_4_out, CLR, and_4_out);
  and and_3 (and_3_out, HR_ADV, SETUP);
  Counter #(.Bits(5)) HOURS_COUNTER (.en(1'b1), .C(or_3_out), .clr(or_4_out), .out(HOURS));  // open: ovf
  and and_4 (and_4_out, HOURS[0], HOURS[1], HOURS[2], HOURS[4]);
endmodule
