// Digital circuit ConventionalAlarmClock.dig as structural Verilog
module ConventionalAlarmClock (
  input  SETUP_TIME,
  input  SETUP_ALARM,
  input  CLK,
  input  CLR,
  input  MIN_ADV,
  input  HR_ADV,
  input  ALARM_EN,
  output [5:0] SECONDS,
  output [5:0] MINUTES,
  output BUZZ,
  output [5:0] ALARM_MINUTES,
  output [4:0] ALARM_HOURS,
  output [13:0] SEG_SECONDS,
  output [13:0] SEG_MINUTES,
  output [13:0] SEG_HOURS,
  output [4:0] HOURS
);

  wire and_1_out, and_2_out, and_3_out, and_4_out, not_1_out, xor_1_out;
  wire [4:0] multiplexer_2_out, xnor_2_out;
  wire [5:0] and_5_out, multiplexer_1_out, multiplexer_3_out, xnor_1_out;

  xor xor_1 (xor_1_out, SETUP_ALARM, SETUP_TIME);
  and and_1 (and_1_out, SETUP_TIME, ~SETUP_ALARM);  // And
  and and_2 (and_2_out, ~SETUP_TIME, SETUP_ALARM);  // And
  and and_3 (and_3_out, CLK, ~xor_1_out, CLK);  // And
  and and_4 (and_4_out, SETUP_ALARM, ~SETUP_TIME);  // And
  BabylonianClock babylonianclock_1 (
    .CLK(and_3_out), .CLR(CLR), .SETUP(and_1_out), .MIN_ADV(MIN_ADV), .HR_ADV(HR_ADV), .SECONDS(SECONDS),
    .MINUTES(MINUTES), .HOURS(HOURS));
  BabylonianAlarm babylonianalarm_1 (
    .CLR(CLR), .SETUP(and_2_out), .MIN_ADV(MIN_ADV), .HR_ADV(HR_ADV), .MINUTES(ALARM_MINUTES),
    .HOURS(ALARM_HOURS));
  assign xnor_1_out = ~(MINUTES ^ ALARM_MINUTES);  // XNOr xnor_1, 6 bits wide
  assign xnor_2_out = ~(HOURS ^ ALARM_HOURS);  // XNOr xnor_2, 5 bits wide
  assign and_5_out = xnor_1_out & {1'b0, xnor_2_out};  // And and_5, 6 bits wide
  Multiplexer #(.Bits(6)) multiplexer_1 (
    .sel(and_4_out), .in_0(MINUTES), .in_1(ALARM_MINUTES), .out(multiplexer_1_out));
  Multiplexer #(.Bits(5)) multiplexer_2 (.sel(and_4_out), .in_0(HOURS), .in_1(ALARM_HOURS), .out(multiplexer_2_out));
  not not_1 (not_1_out, ALARM_EN);
  and and_6 (BUZZ, and_5_out[0], not_1_out);
  Multiplexer #(.Bits(6)) multiplexer_3 (.sel(and_4_out), .in_0(SECONDS), .in_1({6{1'b0}}), .out(multiplexer_3_out));
  SevenSegmentDecoder sevensegmentdecoder_1 (.DATA_IN({1'b0, multiplexer_3_out}), .DATA_OUT(SEG_SECONDS));
  SevenSegmentDecoder sevensegmentdecoder_2 (.DATA_IN({1'b0, multiplexer_1_out}), .DATA_OUT(SEG_MINUTES));
  SevenSegmentDecoder sevensegmentdecoder_3 (.DATA_IN({2'b00, multiplexer_2_out}), .DATA_OUT(SEG_HOURS));
endmodule
