// Digital circuit BabylonianClock.dig as structural Verilog
module BabylonianClock (
  input  CLK,
  input  CLR,
  input  SETUP,
  input  MIN_ADV,
  input  HR_ADV,
  output [5:0] SECONDS,
  output [5:0] MINUTES,
  output [4:0] HOURS
);

  wire and_1_out, and_2_out, and_3_out, and_4_out, and_5_out, and_6_out, and_7_out, and_8_out, or_1_out,
       or_2_out, or_3_out, or_4_out, or_5_out, or_6_out;

  and and_1 (and_1_out, ~SETUP, CLK);  // And
  or or_1 (or_1_out, and_1_out, CLR);
  or or_2 (or_2_out, CLR, and_2_out);
  Counter #(.Bits(6)) SECONDS_COUNTER (.en(1'b1), .C(or_1_out), .clr(or_2_out), .out(SECONDS));  // open: ovf
  and and_2 (and_2_out, SECONDS[0], SECONDS[1], SECONDS[3], SECONDS[4], SECONDS[5]);
  and and_3 (and_3_out, ~and_1_out, and_2_out);  // And
  and and_4 (and_4_out, MIN_ADV, SETUP);
  or or_3 (or_3_out, and_4_out, and_3_out, CLR);
  or or_4 (or_4_out, CLR, and_5_out);
  Counter #(.Bits(6)) MINUTES_COUNTER (.en(1'b1), .C(or_3_out), .clr(or_4_out), .out(MINUTES));  // open: ovf
  and and_5 (and_5_out, MINUTES[0], MINUTES[1], MINUTES[3], MINUTES[4], MINUTES[5]);
  and and_6 (and_6_out, ~or_3_out, and_5_out);  // And
  or or_5 (or_5_out, and_7_out, and_6_out, CLR);
  or or_6 (or_6_out, CLR, and_8_out);
  and and_7 (and_7_out, HR_ADV, SETUP);
  Counter #(.Bits(5)) HOURS_COUNTER (.en(1'b1), .C(or_5_out), .clr(or_6_out), .out(HOURS));  // open: ovf
  and and_8 (and_8_out, HOURS[0], HOURS[1], HOURS[2], HOURS[4]);

  // Notes on the sheet:
  //   CLK: Hz: 500
endmodule
