// Digital circuit SevenSegmentDecoder.dig as structural Verilog
module SevenSegmentDecoder (
  input  [6:0] DATA_IN,
  output [13:0] DATA_OUT
);

  LookUpTable #(.Bits(14)) SEG_DECODER (
    .in0(DATA_IN[0]), .in1(DATA_IN[1]), .in2(DATA_IN[2]), .in3(DATA_IN[3]), .in4(DATA_IN[4]),
    .in5(DATA_IN[5]), .in6(DATA_IN[6]), .out(DATA_OUT));

  // Notes on the sheet:
  //   contents of SEG_DECODER (hex, n*v repeats v):
  //   1fbf,1f86,1fdb,1fcf,1fe6,1fed,1ffd,1f87,1fff,1fe7,33f,306,35b,34f,366,36d,37d,307,37f,367,2dbf,
  //   2d86,2ddb,2dcf,2de6,2ded,2dfd,2d87,2dff,2de7,27bf,2786,27db,27cf,27e6,27ed,27fd,2787,27ff,27e7,
  //   333f,3306,335b,334f,3366,336d,337d,3307,337f,3367,36bf,3686,36db,36cf,36e6,36ed,36fd,3687,36ff,
  //   36e7,3ebf,3e86,3edb,3ecf,3ee6,3eed,3efd,3e87,3eff,3ee7,3bf,386,3db,3cf,3e6,3ed,3fd,387,3ff,
  //   3e7,3fbf,3f86,3fdb,3fcf,3fe6,3fed,3ffd,3f87,3fff,3fe7,33bf,3386,33db,33cf,33e6,33ed,33fd,3387,
  //   33ff,33e7,
endmodule
